# Fritzing sketch Pixelit (saved by Fritzing 0.9.4)

parts:
  WeMos_D1_Mini2 = WeMos D1 Mini
  WS2812B_LED_Matrix = WS2812 RGB LED matrix 4x4
  DHT22 = DHT22 Humidity and Temperature Sensor
  R3 = Resistor [tolerance=±5% resistance=10k package="0603 [SMD]"]
  DFPlayer_Mini = DFPlayer MINI [package="DIP (Dual Inline) [THT]"]
  5V_Power_in = Power plug
  1000uF = Capacitor Polarized [package=cpol-radial-1000uf-25v]
  GL5516 = Photocell (LDR) [package=THT]
  WeMos_D1_Mini4 = WeMos D1 Mini
  R2 = Resistor [tolerance=±5% resistance=4.7k package="0603 [SMD]"]
  WeMos_D1_Mini5 = WeMos D1 Mini
  BME280 = BME280 Breakout
  WeMos_D1_Mini6 = WeMos D1 Mini
  WeMos_D1_Mini = WeMos D1 Mini
  WeMos_D1_Mini7 = WeMos D1 Mini
  Bauteil1 = Adafruit BME680
  WeMos_D1_Mini8 = WeMos D1 Mini
  Btn_1 = TTP223B Capacitive Touch Sensor Module
  Btn_2 = TTP223B Capacitive Touch Sensor Module
  Btn_3 = TTP223B Capacitive Touch Sensor Module

nets:
  VCC: WeMos_D1_Mini2.5V, WS2812B_LED_Matrix.VCC, 5V_Power_in.VCC, 1000uF.-
  N1: WeMos_D1_Mini2.D2, WS2812B_LED_Matrix.DIN
  GND: WeMos_D1_Mini2.G, WS2812B_LED_Matrix.GND, 5V_Power_in.GND, 1000uF.+
  VDD: DHT22.VDD, WeMos_D1_Mini4.3V3, R2.Pin_1
  N2: DHT22.DATA, DHT22.NULL, WeMos_D1_Mini4.D1, R2.Pin_0
  N3: DHT22.GND, WeMos_D1_Mini4.G
  N4: R3.Pin_0, WeMos_D1_Mini.A0
  N5: R3.Pin_1, WeMos_D1_Mini.G
  VCC_2: DFPlayer_Mini.VCC, WeMos_D1_Mini6.3V3
  N6: DFPlayer_Mini.RX, WeMos_D1_Mini6.D5
  N7: DFPlayer_Mini.TX, WeMos_D1_Mini6.D7
  N8: DFPlayer_Mini.GND, WeMos_D1_Mini6.G
  N9: GL5516.pin_0, WeMos_D1_Mini.3V3
  3V3: WeMos_D1_Mini5.3V3, BME280.3.3V
  N10: WeMos_D1_Mini5.D1, BME280.SCK/SCL
  N11: WeMos_D1_Mini5.D3, BME280.SDI/SDA
  N12: WeMos_D1_Mini5.G, BME280.GND
  3V3_2: WeMos_D1_Mini7.3V3, Bauteil1.3.3V
  N13: WeMos_D1_Mini7.D1, Bauteil1.SCK/SCL
  N14: WeMos_D1_Mini7.D3, Bauteil1.SDI/SDA
  N15: WeMos_D1_Mini7.G, Bauteil1.GND
  VCC_3: WeMos_D1_Mini8.3V3, Btn_1.VCC, Btn_2.VCC, Btn_3.VCC
  N16: WeMos_D1_Mini8.D0, Btn_1.SIG
  N17: WeMos_D1_Mini8.D4, Btn_2.SIG
  N18: WeMos_D1_Mini8.D8, Btn_3.SIG
  N19: WeMos_D1_Mini8.G, Btn_3.GND
  GND_2: Btn_1.GND, Btn_2.GND

notes:
  Active High
  Active Low

custom parts:
  WS2812 RGB LED matrix 4x4: WS2812 matrix 4x4
  DFPlayer MINI: MP3 module by DFRobot.com for playing Music from an SD-Card. Supports WAV and MP3 files.
  TTP223B Capacitive Touch Sensor Module: The TTP223B capacitive touch sensor module uses the TTP223B IC. The appropriate voltage is approximately 2 to 5.5 volts.
